// Logisim project Hydrosure_logisim_file.circ as structural Verilog: 1 circuit, main circuit main
module main (
  input  in_1,
  input  in_2,
  input  in_3,
  input  in_4,
  input  in_5,
  input  in_6,
  input  in_7,
  input  in_8,
  input  in_9,
  input  in_10,
  input  in_11,
  input  in_12,
  input  in_13,
  input  in_14,
  input  in_15,
  input  in_16,
  input  in_17,
  input  in_18,
  input  in_19,
  input  in_20,
  input  in_21,
  input  in_22,
  input  in_23,
  input  in_24,
  input  in_25,
  input  in_26,
  input  in_27,
  input  A3,
  input  B3,
  input  REVERSER,
  output out_31,
  output out_32,
  output out_33,
  output out_34,
  output out_35,
  output out_36,
  output out_37,
  output out_38,
  output out_39,
  output out_40,
  output out_41,
  output out_42,
  output out_43,
  output out_44,
  output out_45,
  output So,
  output S1,
  output S2,
  output S3,
  output out_50
);

  wire adder_1_cout, adder_2_cout, adder_3_cout, and_1_out, and_2_out, and_3_out, and_4_out, and_5_out,
       and_6_out, and_7_out, button_1_out, not_1_out, or_1_out, or_2_out, or_3_out, or_4_out, or_5_out,
       priority_encoder_1_en_out, priority_encoder_2_en_out, t_ff_1_q, t_ff_1_qn, t_ff_2_q, t_ff_2_qn,
       t_ff_3_q, t_ff_3_qn, undriven, undriven_2;

  Button button_1 (.out(button_1_out));
  Priority_Encoder #(.select(4)) priority_encoder_1 (
    .in0(in_1), .in1(in_2), .in2(in_3), .in3(in_4), .in4(in_5), .in5(in_6), .in6(in_7), .in7(in_8),
    .in8(in_9), .in9(in_10), .in10(in_11), .in11(in_12), .in12(in_14), .in13(in_15), .in14(in_16),
    .in15(in_17), .out({out_32, out_33, out_34, out_35}), .gs(out_36), .en_out(priority_encoder_1_en_out),
    .en_in(undriven_2));
  Priority_Encoder priority_encoder_2 (
    .in0(in_18), .in1(in_19), .in2(in_20), .in3(in_21), .in4(in_22), .in5(in_23), .in6(in_25), .in7(in_27),
    .out({out_42, out_43, out_44}), .en_in(undriven), .gs(out_45), .en_out(priority_encoder_2_en_out));
  T_Flip_Flop t_ff_1 (.clk(button_1_out), .T(or_2_out), .Q(t_ff_1_q), .Qn(t_ff_1_qn));  // open: preset, reset, en
  not not_1 (not_1_out, REVERSER);
  and and_1 (and_1_out, not_1_out, t_ff_1_qn, t_ff_2_q, t_ff_3_q);
  LED led_1 (.in(t_ff_1_q));
  LED led_2 (.in(t_ff_2_q));
  and and_2 (and_2_out, REVERSER, t_ff_1_qn, t_ff_2_q, t_ff_3_qn);
  and and_3 (and_3_out, and_6_out, t_ff_3_q);
  T_Flip_Flop t_ff_2 (.clk(button_1_out), .T(or_3_out), .Q(t_ff_2_q), .Qn(t_ff_2_qn));  // open: preset, reset, en
  or or_1 (or_1_out, REVERSER, t_ff_1_q);
  LED led_3 (.in(t_ff_3_q));
  or or_2 (or_2_out, and_4_out, and_1_out);
  Adder #(.width(1)) adder_1 (.a(out_44), .b(t_ff_3_q), .out(So), .cin(in_24), .cout(adder_1_cout));
  Adder #(.width(1)) adder_2 (.a(out_43), .b(t_ff_2_q), .out(S1), .cin(adder_1_cout), .cout(adder_2_cout));
  Adder #(.width(1)) adder_3 (.a(out_42), .b(t_ff_1_q), .out(S2), .cin(adder_2_cout), .cout(adder_3_cout));
  Adder #(.width(1)) adder_4 (.a(A3), .b(B3), .out(S3), .cin(adder_3_cout), .cout(out_50));
  or or_3 (or_3_out, and_3_out, and_2_out, and_5_out);
  and and_4 (and_4_out, t_ff_2_qn, or_1_out, t_ff_3_qn);
  and and_5 (and_5_out, REVERSER, t_ff_1_q, t_ff_2_qn, t_ff_3_qn);
  or or_4 (or_4_out, and_5_out, and_6_out, and_7_out);
  T_Flip_Flop t_ff_3 (.clk(button_1_out), .T(or_4_out), .Q(t_ff_3_q), .Qn(t_ff_3_qn));  // open: preset, reset, en
  or or_5 (or_5_out, t_ff_3_q, t_ff_2_q);
  and and_6 (and_6_out, not_1_out, t_ff_1_qn);
  and and_7 (and_7_out, REVERSER, t_ff_1_qn, or_5_out);
  Comparator #(.width(4), .mode("unsigned")) comparator_1 (
    .a({out_32, out_33, out_34, out_35}), .b({S3, S2, S1, So}), .gt(out_37), .eq(out_38), .lt(out_40));
  xor xor_1 (out_39, out_38, out_40);

  // Notes on the sheet:
  //   EC129:   Md Atib Kaif
  //   EC130:   Medhinee
  //   OUTPUTS FROM
  //   MOISTURE SENSOR
  //   OUTPUTS FROM
  //   TEMPERATURE
  //   SENSOR
  //   CROP-SELECTOR
  //   PUSH - BUTTON
  //   4 - BIT PRIORITY ENCODER
  //   3 - BIT PRIORITY ENCODER
  //   HYROSURE
  //   MOISTURE SENSING CUM WATERING SYSTEM
  //   CROP NUMBER
  //   Ao
  //   Bo
  //   A1
  //   B1
  //   A2
  //   B2
  //   4 - BIT ADDER
  //   4 - BIT COMPARATOR
  //   FINAL OUTPUT
endmodule
